# Fritzing sketch LED Flash - PIR (saved by Fritzing 0.9.7b)
breadboards: 1

parts:
  Raspberry_Pi_1 = Raspberry Pi 3 [part_number=RPI-3-V1.2]
  LED1 = LED - 5mm [color="Red (633nm)" current=0.030 package="5 mm [THT]"]
  R1 = Resistor [tolerance=±5% power=0.25 resistance=220 package=THT]
  PIR1 = PIR sensor

nets:
  N1: Raspberry_Pi_1.GIPO17, LED1.anode
  N2: Raspberry_Pi_1.GIPO27, PIR1.SIG
  GND: Raspberry_Pi_1.GND, R1.Pin_0, PIR1.GND
  5V: Raspberry_Pi_1.5V, PIR1.VDD
  N3: LED1.cathode, R1.Pin_1
